# Fritzing sketch Pico DHT11 (saved by Fritzing 1.0.1rc)
breadboards: 1

parts:
  DHT1 = Humidity and Temperature Sensor DHT11 [part_number=DHT11]  # not connected
  Pico_H1 = Raspberry Pi Pico H

nets:
  N1: Pico_H1.VSYS, Pico_H1.GP21, Pico_H1.GP7
  N2: Pico_H1.ADC_VREF, Pico_H1.GP18
  N3: Pico_H1.AGND, Pico_H1.GP11
  N4: Pico_H1.GND, Pico_H1.GP2

custom parts:
  Humidity and Temperature Sensor DHT11: DHT11 digital temperature and humidity sensor is a composite Sensor contains a calibrated digital signal output of the temperature and humidity. Application of a dedicated digital modules collection technology and the temperature and humidity sensing technology, to ensure that the product has high reliability and excellent long term stability. The sensor includes a resistive sense of wet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
  Raspberry Pi Pico H: Raspberry Pi Pico H. Based around the RP2040 microcontroller the Pico H is a low cost microcontroller device bringing Raspberry Pi quality, cost, and easy of use to the microcontroller space.
