# Fritzing sketch Pico 18B20 (saved by Fritzing 1.0.1rc)
breadboards: 1

parts:
  Pico_H1 = Raspberry Pi Pico H
  DS1 = DS18B20 Temperature Sensor [part_number=DS18B20]
  Part1 = Adafruit DRV8833 DC/Stepper Motor Driver [part_number="Adafruit #3297"]
  M1 = DC Motor [voltage_(max)=6V voltage_(min)=3V]

nets:
  N1: Pico_H1.VSYS, Pico_H1.GP21, Pico_H1.GP7, DS1.R/VCC, Part1.PWRIN
  N2: Pico_H1.ADC_VREF, Pico_H1.GP18
  N3: Pico_H1.AGND, Pico_H1.GP19, Pico_H1.GP11, DS1.G/GND, Part1.GND
  N4: Pico_H1.GP14, Part1.AIN1
  N5: Pico_H1.GND, Pico_H1.GP2
  N6: Pico_H1.GP9, DS1.Y/DQ
  N7: Part1.AOUT1, M1.pin_1

custom parts:
  Raspberry Pi Pico H: Raspberry Pi Pico H. Based around the RP2040 microcontroller the Pico H is a low cost microcontroller device bringing Raspberry Pi quality, cost, and easy of use to the microcontroller space.
  DS18B20 Temperature Sensor: The DS18B20 digital thermometer provides 9-bit to 12-bit Celsius temperature measurements and has an alarm function with nonvolatile user-programmable upper and lower trigger points. The DS18B20 communicates over a 1-Wire bus that by definition requires only one data line (and ground) for communication with a central microprocessor. In addition, the DS18B20 can derive power directly from the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
  Adafruit DRV8833 DC/Stepper Motor Driver: Spin two DC motors or step one bi-polar or uni-polar stepper with up to 1.2A per channel using the DRV8833. This motor driver chip is a nice alternative to the TB6612 driver. Like that chip, you get 2 full H-bridges, but this chip is better for low voltage uses (can run from 2.7V up to 10.8V motor power) and has built in current limiting capability. We set it up for 1A current limiting so you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
