# Fritzing sketch Pico push button (saved by Fritzing 1.0.1rc)
breadboards: 1

parts:
  Pico_H1 = Raspberry Pi Pico H
  S1 = Push button breakout

nets:
  N1: Pico_H1.VSYS, Pico_H1.GP21, Pico_H1.GP7
  N2: Pico_H1.ADC_VREF, Pico_H1.GP18
  N3: Pico_H1.AGND, Pico_H1.GP11
  N4: Pico_H1.GND, Pico_H1.GP2
  N5: S1.S, S1.VCC

custom parts:
  Raspberry Pi Pico H: Raspberry Pi Pico H. Based around the RP2040 microcontroller the Pico H is a low cost microcontroller device bringing Raspberry Pi quality, cost, and easy of use to the microcontroller space.
  Push button breakout: Elgoo sensor kit breakout with a push to make button
